// Logisim project CompleteMips.circ as structural Verilog: 17 circuits, main circuit Final?
module main (
);

  wire alu_1_p3, alu_1_p4, and_1_out, controlunit_1_p2, controlunit_1_p3, controlunit_1_p4, controlunit_1_p5,
       controlunit_1_p6, controlunit_1_p7, controlunit_1_p8, controlunit_1_p9, controlunit_1_p10,
       controlunit_1_p11, registerfile_1_p6;
  wire [1:0] not_1_out;
  wire [4:0] registerfile_1_p3;
  wire [7:0] multiplexer_6_out;
  wire [31:0] adder_1_out, adder_2_out, alu_1_p2, alu_1_p5, bit_extender_1_out, bit_extender_2_out,
       datamemory_1_out_5, instructionmemory_1_out_2, multiplexer_3_out, multiplexer_4_out,
       multiplexer_5_out, multiplexer_8_out, n2bitshift_1_out_2, pc_1_out_2, registerfile_1_p4,
       registerfile_1_p7, shifter_1_out, shifter_2_out, shifter_3_out, undriven;

  PC pc_1 (.in_1(multiplexer_3_out), .out_2(pc_1_out_2));
  Adder #(.width(32)) adder_1 (.a(pc_1_out_2), .b(32'h4), .out(adder_1_out));  // open: cin, cout
  InstructionMemory instructionmemory_1 (.in_1(pc_1_out_2), .out_2(instructionmemory_1_out_2));
  // ControlUnit controlunit_1: pin names not known; wires that end beside it: instructionmemory_1_out_2[31:26], controlunit_1_p2, controlunit_1_p3, controlunit_1_p4, controlunit_1_p5, controlunit_1_p6, controlunit_1_p7, controlunit_1_p8, controlunit_1_p9, controlunit_1_p10, controlunit_1_p11
  // RegisterFile registerfile_1: pin names not known; wires that end beside it: instructionmemory_1_out_2[25:21], instructionmemory_1_out_2[20:16], registerfile_1_p3, registerfile_1_p4, controlunit_1_p10, registerfile_1_p6, registerfile_1_p7
  Multiplexer #(.width(5), .enable("false")) multiplexer_1 (
    .in0(instructionmemory_1_out_2[20:16]), .in1(instructionmemory_1_out_2[15:11]), .out(registerfile_1_p3),
    .sel(controlunit_1_p2));
  assign bit_extender_1_out = {{16{instructionmemory_1_out_2[15]}}, instructionmemory_1_out_2[15:0]};  // Bit_Extender bit_extender_1
  _2BitShift u_2bitshift_1 (.in_1(bit_extender_1_out), .out_2(n2bitshift_1_out_2));
  // ALU alu_1: pin names not known; wires that end beside it: registerfile_1_p6, alu_1_p2, alu_1_p3, alu_1_p4, alu_1_p5, alu_1_p5
  Multiplexer #(.width(32), .enable("false")) multiplexer_2 (
    .in0(registerfile_1_p7), .in1(bit_extender_1_out), .out(alu_1_p2), .sel(controlunit_1_p9));
  // ALU_Control alu_control_1: pin names not known; wires that end beside it: instructionmemory_1_out_2[5:0], controlunit_1_p7, alu_1_p3
  Adder #(.width(32)) adder_2 (.a(adder_1_out), .b(n2bitshift_1_out_2), .out(adder_2_out));  // open: cin, cout
  and and_1 (and_1_out, controlunit_1_p4, alu_1_p4);
  Multiplexer #(.width(32), .enable("false")) multiplexer_3 (
    .in0(adder_1_out), .in1(adder_2_out), .out(multiplexer_3_out), .sel(and_1_out));
  Multiplexer #(.width(32), .enable("false")) multiplexer_4 (
    .in0(undriven), .in1(shifter_1_out), .out(multiplexer_4_out));  // open: sel
  Shifter #(.width(32)) shifter_1 (.in(undriven), .\dist (5'b01000), .out(shifter_1_out));
  DataMemory datamemory_1 (
    .in_2({alu_1_p5[31:2], 2'b00}), .in_3(registerfile_1_p7), .out_5(datamemory_1_out_5));  // open: in_1, in_4
  Multiplexer #(.width(32), .enable("false")) multiplexer_5 (
    .in0(multiplexer_4_out), .in1(shifter_2_out), .out(multiplexer_5_out));  // open: sel
  Shifter #(.width(32)) shifter_2 (.in(multiplexer_4_out), .\dist (5'b01000), .out(shifter_2_out));
  assign not_1_out = ~alu_1_p5[1:0];  // NOT_Gate not_1, 2 bits wide
  Multiplexer #(.select(2), .width(8), .enable("false")) multiplexer_6 (
    .in0(datamemory_1_out_5[7:0]), .in1(datamemory_1_out_5[15:8]), .in2(datamemory_1_out_5[23:16]),
    .in3(datamemory_1_out_5[31:24]), .out(multiplexer_6_out), .sel(not_1_out));
  Multiplexer #(.width(32), .enable("false")) multiplexer_7 (
    .in0(multiplexer_5_out), .in1(shifter_3_out));  // open: out, sel
  Shifter #(.width(32)) shifter_3 (.in(multiplexer_5_out), .\dist (5'b01000), .out(shifter_3_out));
  assign bit_extender_2_out = {{24{multiplexer_6_out[7]}}, multiplexer_6_out};  // Bit_Extender bit_extender_2
  Multiplexer #(.width(32), .enable("false")) multiplexer_8 (
    .in0(datamemory_1_out_5), .in1(bit_extender_2_out), .out(multiplexer_8_out), .sel(controlunit_1_p11));
  Multiplexer #(.width(32), .enable("false")) multiplexer_9 (
    .in0(alu_1_p5), .in1(multiplexer_8_out), .out(registerfile_1_p4), .sel(controlunit_1_p6));
endmodule

module RegisterFile (
  input  WRITE,
  input  [31:0] Write_Data,
  input  [4:0] in_3,
  input  [4:0] in_4,
  input  [4:0] in_5,
  output [31:0] out_6,
  output [31:0] out_7
);

  wire and_1_out, and_2_out, and_3_out, and_4_out, and_5_out, and_6_out, and_7_out, and_8_out, and_9_out,
       and_10_out, and_11_out, and_12_out, and_13_out, and_14_out, and_15_out, and_16_out, and_17_out,
       and_18_out, and_19_out, and_20_out, and_21_out, and_22_out, and_23_out, and_24_out, and_25_out,
       and_26_out, and_27_out, and_28_out, and_29_out, and_30_out, and_31_out, and_32_out, decoder_1_out0,
       decoder_1_out1, decoder_1_out2, decoder_1_out3, decoder_1_out4, decoder_1_out5, decoder_1_out6,
       decoder_1_out7, decoder_1_out8, decoder_1_out9, decoder_1_out10, decoder_1_out11, decoder_1_out12,
       decoder_1_out13, decoder_1_out14, decoder_1_out15, decoder_1_out16, decoder_1_out17, decoder_1_out18,
       decoder_1_out19, decoder_1_out20, decoder_1_out21, decoder_1_out22, decoder_1_out23, decoder_1_out24,
       decoder_1_out25, decoder_1_out26, decoder_1_out27, decoder_1_out28, decoder_1_out29, decoder_1_out30,
       decoder_1_out31, undriven;
  wire [31:0] register_1_q, register_2_q, register_3_q, register_4_q, register_5_q, register_6_q,
       register_7_q, register_8_q, register_9_q, register_10_q, register_11_q, register_12_q, register_13_q,
       register_14_q, register_15_q, register_16_q, register_17_q, register_18_q, register_19_q,
       register_20_q, register_21_q, register_22_q, register_23_q, register_24_q, register_25_q,
       register_26_q, register_27_q, register_28_q, register_29_q, register_30_q, register_31_q,
       register_32_q;

  Decoder #(.select(5)) decoder_1 (
    .out0(decoder_1_out0), .out1(decoder_1_out1), .out2(decoder_1_out2), .out3(decoder_1_out3),
    .out4(decoder_1_out4), .out5(decoder_1_out5), .out6(decoder_1_out6), .out7(decoder_1_out7),
    .out8(decoder_1_out8), .out9(decoder_1_out9), .out10(decoder_1_out10), .out11(decoder_1_out11),
    .out12(decoder_1_out12), .out13(decoder_1_out13), .out14(decoder_1_out14), .out15(decoder_1_out15),
    .out16(decoder_1_out16), .out17(decoder_1_out17), .out18(decoder_1_out18), .out19(decoder_1_out19),
    .out20(decoder_1_out20), .out21(decoder_1_out21), .out22(decoder_1_out22), .out23(decoder_1_out23),
    .out24(decoder_1_out24), .out25(decoder_1_out25), .out26(decoder_1_out26), .out27(decoder_1_out27),
    .out28(decoder_1_out28), .out29(decoder_1_out29), .out30(decoder_1_out30), .out31(decoder_1_out31),
    .sel(in_3), .en(undriven));
  and and_1 (and_1_out, decoder_1_out0, WRITE);
  and and_2 (and_2_out, decoder_1_out1, WRITE);
  and and_3 (and_3_out, decoder_1_out2, WRITE);
  and and_4 (and_4_out, decoder_1_out3, WRITE);
  and and_5 (and_5_out, decoder_1_out4, WRITE);
  and and_6 (and_6_out, decoder_1_out5, WRITE);
  and and_7 (and_7_out, decoder_1_out6, WRITE);
  and and_8 (and_8_out, decoder_1_out7, WRITE);
  and and_9 (and_9_out, decoder_1_out8, WRITE);
  and and_10 (and_10_out, decoder_1_out9, WRITE);
  and and_11 (and_11_out, decoder_1_out10, WRITE);
  and and_12 (and_12_out, decoder_1_out11, WRITE);
  and and_13 (and_13_out, decoder_1_out12, WRITE);
  and and_14 (and_14_out, decoder_1_out13, WRITE);
  and and_15 (and_15_out, decoder_1_out14, WRITE);
  and and_16 (and_16_out, decoder_1_out15, WRITE);
  and and_17 (and_17_out, decoder_1_out16, WRITE);
  and and_18 (and_18_out, decoder_1_out17, WRITE);
  and and_19 (and_19_out, decoder_1_out18, WRITE);
  and and_20 (and_20_out, decoder_1_out19, WRITE);
  and and_21 (and_21_out, decoder_1_out20, WRITE);
  and and_22 (and_22_out, decoder_1_out21, WRITE);
  and and_23 (and_23_out, decoder_1_out22, WRITE);
  and and_24 (and_24_out, decoder_1_out23, WRITE);
  and and_25 (and_25_out, decoder_1_out24, WRITE);
  and and_26 (and_26_out, decoder_1_out25, WRITE);
  and and_27 (and_27_out, decoder_1_out26, WRITE);
  and and_28 (and_28_out, decoder_1_out27, WRITE);
  and and_29 (and_29_out, decoder_1_out28, WRITE);
  and and_30 (and_30_out, decoder_1_out29, WRITE);
  and and_31 (and_31_out, decoder_1_out30, WRITE);
  and and_32 (and_32_out, decoder_1_out31, WRITE);
  Register #(.width(32)) register_1 (.D(Write_Data), .en(and_1_out), .Q(register_1_q), .clk(undriven));  // open: clr
  Register #(.width(32)) register_2 (.D(Write_Data), .en(and_2_out), .Q(register_2_q), .clk(undriven));  // open: clr
  Register #(.width(32)) register_3 (.D(Write_Data), .en(and_3_out), .Q(register_3_q), .clk(undriven));  // open: clr
  Register #(.width(32)) register_4 (.D(Write_Data), .en(and_4_out), .Q(register_4_q), .clk(undriven));  // open: clr
  Register #(.width(32)) register_5 (.D(Write_Data), .en(and_5_out), .Q(register_5_q), .clk(undriven));  // open: clr
  Register #(.width(32)) register_6 (.D(Write_Data), .en(and_6_out), .Q(register_6_q), .clk(undriven));  // open: clr
  Register #(.width(32)) register_7 (.D(Write_Data), .en(and_7_out), .Q(register_7_q), .clk(undriven));  // open: clr
  Register #(.width(32)) register_8 (.D(Write_Data), .en(and_8_out), .Q(register_8_q), .clk(undriven));  // open: clr
  Register #(.width(32)) register_9 (.D(Write_Data), .en(and_9_out), .Q(register_9_q), .clk(undriven));  // open: clr
  Register #(.width(32)) register_10 (.D(Write_Data), .en(and_10_out), .Q(register_10_q), .clk(undriven));  // open: clr
  Register #(.width(32)) register_11 (.D(Write_Data), .en(and_11_out), .Q(register_11_q), .clk(undriven));  // open: clr
  Register #(.width(32)) register_12 (.D(Write_Data), .en(and_12_out), .Q(register_12_q), .clk(undriven));  // open: clr
  Register #(.width(32)) register_13 (.D(Write_Data), .en(and_13_out), .Q(register_13_q), .clk(undriven));  // open: clr
  Register #(.width(32)) register_14 (.D(Write_Data), .en(and_14_out), .Q(register_14_q), .clk(undriven));  // open: clr
  Register #(.width(32)) register_15 (.D(Write_Data), .en(and_15_out), .Q(register_15_q), .clk(undriven));  // open: clr
  Register #(.width(32)) register_16 (.D(Write_Data), .en(and_16_out), .Q(register_16_q), .clk(undriven));  // open: clr
  Register #(.width(32)) register_17 (.D(Write_Data), .en(and_17_out), .Q(register_17_q), .clk(undriven));  // open: clr
  Register #(.width(32)) register_18 (.D(Write_Data), .en(and_18_out), .Q(register_18_q), .clk(undriven));  // open: clr
  Register #(.width(32)) register_19 (.D(Write_Data), .en(and_19_out), .Q(register_19_q), .clk(undriven));  // open: clr
  Register #(.width(32)) register_20 (.D(Write_Data), .en(and_20_out), .Q(register_20_q), .clk(undriven));  // open: clr
  Register #(.width(32)) register_21 (.D(Write_Data), .en(and_21_out), .Q(register_21_q), .clk(undriven));  // open: clr
  Register #(.width(32)) register_22 (.D(Write_Data), .en(and_22_out), .Q(register_22_q), .clk(undriven));  // open: clr
  Register #(.width(32)) register_23 (.D(Write_Data), .en(and_23_out), .Q(register_23_q), .clk(undriven));  // open: clr
  Register #(.width(32)) register_24 (.D(Write_Data), .en(and_24_out), .Q(register_24_q), .clk(undriven));  // open: clr
  Register #(.width(32)) register_25 (.D(Write_Data), .en(and_25_out), .Q(register_25_q), .clk(undriven));  // open: clr
  Register #(.width(32)) register_26 (.D(Write_Data), .en(and_26_out), .Q(register_26_q), .clk(undriven));  // open: clr
  Register #(.width(32)) register_27 (.D(Write_Data), .en(and_27_out), .Q(register_27_q), .clk(undriven));  // open: clr
  Register #(.width(32)) register_28 (.D(Write_Data), .en(and_28_out), .Q(register_28_q), .clk(undriven));  // open: clr
  Register #(.width(32)) register_29 (.D(Write_Data), .en(and_29_out), .Q(register_29_q), .clk(undriven));  // open: clr
  Register #(.width(32)) register_30 (.D(Write_Data), .en(and_30_out), .Q(register_30_q), .clk(undriven));  // open: clr
  Register #(.width(32)) register_31 (.D(Write_Data), .en(and_31_out), .Q(register_31_q), .clk(undriven));  // open: clr
  Register #(.width(32)) register_32 (.D(Write_Data), .en(and_32_out), .Q(register_32_q), .clk(undriven));  // open: clr
  Multiplexer #(.select(5), .width(32)) multiplexer_1 (
    .in0(register_1_q), .in1(register_2_q), .in2(register_3_q), .in3(register_4_q), .in4(register_5_q),
    .in5(register_6_q), .in6(register_7_q), .in7(register_8_q), .in8(register_9_q), .in9(register_10_q),
    .in10(register_11_q), .in11(register_12_q), .in12(register_13_q), .in13(register_14_q),
    .in14(register_15_q), .in15(register_16_q), .in16(register_17_q), .in17(register_18_q),
    .in18(register_19_q), .in19(register_20_q), .in20(register_21_q), .in21(register_22_q),
    .in22(register_23_q), .in23(register_24_q), .in24(register_25_q), .in25(register_26_q),
    .in26(register_27_q), .in27(register_28_q), .in28(register_29_q), .in29(register_30_q),
    .in30(register_31_q), .in31(register_32_q), .out(out_6), .sel(in_4), .en(undriven));
  Multiplexer #(.select(5), .width(32)) multiplexer_2 (
    .in0(register_1_q), .in1(register_2_q), .in2(register_3_q), .in3(register_4_q), .in4(register_5_q),
    .in5(register_6_q), .in6(register_7_q), .in7(register_8_q), .in8(register_9_q), .in9(register_10_q),
    .in10(register_11_q), .in11(register_12_q), .in12(register_13_q), .in13(register_14_q),
    .in14(register_15_q), .in15(register_16_q), .in16(register_17_q), .in17(register_18_q),
    .in18(register_19_q), .in19(register_20_q), .in20(register_21_q), .in21(register_22_q),
    .in22(register_23_q), .in23(register_24_q), .in24(register_25_q), .in25(register_26_q),
    .in26(register_27_q), .in27(register_28_q), .in28(register_29_q), .in29(register_30_q),
    .in30(register_31_q), .in31(register_32_q), .out(out_7), .sel(in_5), .en(undriven));

  // Notes on the sheet:
  //   Clock
endmodule

module ALU (
  input  in_1,
  input  in_2,
  input  in_3,
  input  [31:0] in_4,
  input  [31:0] in_5,
  input  [3:0] in_6,
  input  [4:0] in_7,
  output out_8,
  output [31:0] out_9
);

  wire comparator_1_lt;
  wire [31:0] adder_1_out, and_1_out, bit_extender_1_out, multiplexer_1_out, nor_1_out, or_1_out,
       subtractor_1_out;

  assign and_1_out = in_4 & in_5;  // AND_Gate and_1, 32 bits wide
  assign or_1_out = in_4 | in_5;  // OR_Gate or_1, 32 bits wide
  Adder #(.width(32)) adder_1 (.a(in_4), .b(in_5), .out(adder_1_out));  // open: cin, cout
  Subtractor #(.width(32)) subtractor_1 (.a(in_4), .b(in_5), .out(subtractor_1_out));  // open: bin, bout
  Comparator #(.width(32)) comparator_1 (.a(in_4), .b(in_5), .lt(comparator_1_lt));  // open: gt, eq
  assign nor_1_out = ~(in_4 | in_5);  // NOR_Gate nor_1, 32 bits wide
  assign bit_extender_1_out = {{31{1'b0}}, comparator_1_lt};  // Bit_Extender bit_extender_1
  Multiplexer #(.select(4), .width(32)) multiplexer_1 (
    .in0(and_1_out), .in1(or_1_out), .in2(adder_1_out), .in6(subtractor_1_out), .in7(bit_extender_1_out),
    .in12(nor_1_out), .out(multiplexer_1_out), .sel(in_6), .en(1'b1));  // open: in3, in4, in5, in8, in9, in10, in11, in13, in14, in15
  Shifter #(.width(32)) shifter_1 (.in(multiplexer_1_out), .\dist (in_7), .out(out_9));
  Comparator #(.width(32)) comparator_2 (.a({32{1'b0}}), .b(out_9), .eq(out_8));  // open: gt, lt
endmodule

module InstructionMemory (
  input  [31:0] in_1,
  output [31:0] out_2
);
endmodule

module PC (
  input  [31:0] in_1,
  output [31:0] out_2
);

  wire clock_1_out;

  Register #(.width(32)) register_1 (.D(in_1), .en(1'b1), .Q(out_2), .clk(clock_1_out));  // open: clr
  Clock clock_1 (.out(clock_1_out));
endmodule

module _2BitShift (
  input  [31:0] in_1,
  output [31:0] out_2
);

  Shifter #(.width(32)) shifter_1 (.in(in_1), .\dist (5'b00010), .out(out_2));
endmodule

module ALU_Control (
  input  [5:0] in_1,
  input  [1:0] in_2,
  output out_3,
  output [3:0] out_4,
  output out_5,
  output out_6,
  output out_7,
  output out_8,
  output out_9,
  output out_10,
  output out_11,
  output out_12,
  output out_13,
  output out_14
);
endmodule

module DataMemory (
  input  in_1,
  input  [31:0] in_2,
  input  [31:0] in_3,
  input  in_4,
  output [31:0] out_5
);
endmodule

module ControlUnit (
  input  [5:0] in_1,
  output out_2,
  output out_3,
  output out_4,
  output out_5,
  output out_6,
  output out_7,
  output out_8,
  output out_9,
  output out_10,
  output out_11,
  output out_12,
  output out_13,
  output out_14,
  output out_15,
  output out_16,
  output [1:0] out_17
);
endmodule

module try (
  input  [31:0] in_1,
  output [31:0] out_2,
  output [1:0] out_3
);

  assign out_3 = ~in_1[1:0];  // NOT_Gate not_1, 2 bits wide

  assign out_2 = in_1;
endmodule

module Sign_Extend (
  input  [7:0] in_1,
  input  in_2,
  output [31:0] out_3
);

  wire [31:0] bit_extender_1_out, bit_extender_2_out;

  assign bit_extender_1_out = {{24{1'b0}}, in_1};  // Bit_Extender bit_extender_1
  assign bit_extender_2_out = {{24{in_1[7]}}, in_1};  // Bit_Extender bit_extender_2
  Multiplexer #(.width(32), .enable("false")) multiplexer_1 (
    .in0(bit_extender_1_out), .in1(bit_extender_2_out), .out(out_3), .sel(in_2));
endmodule

module Final (
);

  wire alu_1_out_8, alu_control_1_out_3, alu_control_1_out_5, alu_control_1_out_7, alu_control_1_out_8,
       alu_control_1_out_10, alu_control_1_out_11, alu_control_1_out_12, alu_control_1_out_13,
       alu_control_1_out_14, and_1_out, controlunit_1_out_3, controlunit_1_out_4, controlunit_1_out_5,
       controlunit_1_out_7, controlunit_1_out_8, controlunit_1_out_9, controlunit_1_out_11,
       controlunit_1_out_12, controlunit_1_out_16, not_1_out, RegWrite_out, Signed_out;
  wire [1:0] alu_control_1_out_9, controlunit_1_out_2, controlunit_1_out_6, controlunit_1_out_15,
       controlunit_1_out_17, multiplexer_7_out;
  wire [3:0] alu_control_1_out_4;
  wire [4:0] multiplexer_1_out, multiplexer_4_out;
  wire [5:0] instructionmemory_1_out_2_2;
  wire [25:0] instructionmemory_1_out_2;
  wire [31:0] adder_1_out, adder_2_out, alu_1_out_9, byteextractor_1_out_4, byteextractor_1_out_5,
       datamemory_1_out_5, demultiplexer_1_out0, demultiplexer_1_out1, demultiplexer_2_out0,
       demultiplexer_2_out1, multiplexer_2_out, multiplexer_3_out, multiplexer_5_out, multiplexer_6_out,
       multiplexer_8_out, multiplexer_9_out, multiplexer_10_out, multiplexer_11_out, multiplyunit_1_out_9,
       multiplyunit_1_out_10, n2bitshift_1_out_2, pc_1_out_2, registerfile_1_out_6, registerfile_1_out_7,
       savebyte_1_out_6, signextend1632_1_out_3;

  ControlUnit controlunit_1 (
    .in_1(instructionmemory_1_out_2_2), .out_2(controlunit_1_out_2[0]), .out_3(controlunit_1_out_3),
    .out_4(controlunit_1_out_4), .out_5(controlunit_1_out_5), .out_6(controlunit_1_out_6[0]),
    .out_7(controlunit_1_out_7), .out_17(controlunit_1_out_17), .out_8(controlunit_1_out_8),
    .out_9(controlunit_1_out_9), .out_10(controlunit_1_out_15[1]), .out_11(controlunit_1_out_11),
    .out_12(controlunit_1_out_12), .out_13(alu_control_1_out_9[1]), .out_14(controlunit_1_out_2[1]),
    .out_15(controlunit_1_out_15[0]), .out_16(controlunit_1_out_16));
  ALU_Control alu_control_1 (
    .in_1(instructionmemory_1_out_2[5:0]), .in_2(controlunit_1_out_17), .out_4(alu_control_1_out_4),
    .out_7(alu_control_1_out_7), .out_8(alu_control_1_out_8), .out_9(alu_control_1_out_9[0]),
    .out_11(alu_control_1_out_11), .out_12(alu_control_1_out_12), .out_13(alu_control_1_out_13),
    .out_3(alu_control_1_out_3), .out_5(alu_control_1_out_5), .out_14(alu_control_1_out_14),
    .out_6(controlunit_1_out_6[1]), .out_10(alu_control_1_out_10));
  InstructionMemory instructionmemory_1 (
    .in_1(pc_1_out_2), .out_2({instructionmemory_1_out_2_2, instructionmemory_1_out_2}));
  PC pc_1 (.in_1(multiplexer_8_out), .out_2(pc_1_out_2));
  Adder #(.width(32)) adder_1 (.a(pc_1_out_2), .b(32'h4), .out(adder_1_out));  // open: cin, cout
  or Signed (Signed_out, controlunit_1_out_12, alu_control_1_out_8);
  RegisterFile registerfile_1 (
    .WRITE(RegWrite_out), .Write_Data(multiplexer_2_out), .in_3(multiplexer_1_out),
    .in_4(instructionmemory_1_out_2[25:21]), .in_5(instructionmemory_1_out_2[20:16]),
    .out_6(registerfile_1_out_6), .out_7(registerfile_1_out_7));
  Multiplexer #(.select(2), .width(5), .enable("false")) multiplexer_1 (
    .in0(instructionmemory_1_out_2[20:16]), .in1(instructionmemory_1_out_2[15:11]), .in2({5{1'b1}}),
    .in3({5{1'b1}}), .out(multiplexer_1_out), .sel(controlunit_1_out_2));
  Multiplexer #(.width(32), .enable("false")) multiplexer_2 (
    .in0(demultiplexer_2_out0), .in1(multiplexer_8_out), .out(multiplexer_2_out), .sel(controlunit_1_out_2[1]));
  or RegWrite (RegWrite_out, controlunit_1_out_8, alu_control_1_out_10);
  SignExtend1632 signextend1632_1 (
    .in_1(instructionmemory_1_out_2[15:0]), .in_2(Signed_out), .out_3(signextend1632_1_out_3));
  MultiplyUnit multiplyunit_1 (
    .in_1(demultiplexer_1_out0), .in_2(demultiplexer_1_out1), .in_4(registerfile_1_out_6),
    .in_3(registerfile_1_out_7), .out_9(multiplyunit_1_out_9), .out_10(multiplyunit_1_out_10),
    .in_5(alu_control_1_out_11), .in_6(alu_control_1_out_3), .in_7(alu_control_1_out_12), .in_8(Signed_out));
  Demultiplexer #(.width(32), .enable("false")) demultiplexer_1 (
    .out0(demultiplexer_1_out0), .out1(demultiplexer_1_out1), .in(registerfile_1_out_6),
    .sel(alu_control_1_out_13));
  Multiplexer #(.width(32), .enable("false")) multiplexer_3 (
    .in0(registerfile_1_out_7), .in1(signextend1632_1_out_3), .out(multiplexer_3_out),
    .sel(controlunit_1_out_9));
  Multiplexer #(.select(2), .width(5), .enable("false")) multiplexer_4 (
    .in0({5{1'b0}}), .in1(signextend1632_1_out_3[10:6]), .in2({5{1'b1}}), .in3({5{1'b1}}),
    .out(multiplexer_4_out), .sel(alu_control_1_out_9));
  Multiplexer #(.width(32), .enable("false")) multiplexer_5 (
    .in0(multiplyunit_1_out_9), .in1(multiplyunit_1_out_10), .out(multiplexer_5_out),
    .sel(alu_control_1_out_13));
  ALU alu_1 (
    .in_4(registerfile_1_out_6), .in_5(multiplexer_3_out), .out_9(alu_1_out_9), .out_8(alu_1_out_8),
    .in_6(alu_control_1_out_4), .in_7(multiplexer_4_out), .in_1(alu_control_1_out_5), .in_2(Signed_out),
    .in_3(alu_control_1_out_14));
  Multiplexer #(.width(32), .enable("false")) multiplexer_6 (
    .in0({adder_1_out[31:28], instructionmemory_1_out_2_2[1:0], instructionmemory_1_out_2[25:2], adder_1_out[1:0]}),
    .in1(registerfile_1_out_6), .out(multiplexer_6_out), .sel(alu_control_1_out_7));
  _2BitShift u_2bitshift_1 (.in_1(signextend1632_1_out_3), .out_2(n2bitshift_1_out_2));
  not not_1 (not_1_out, and_1_out);
  and and_1 (and_1_out, controlunit_1_out_3, alu_1_out_8);
  Adder #(.width(32)) adder_2 (.a(adder_1_out), .b(n2bitshift_1_out_2), .out(adder_2_out));  // open: cin, cout
  Multiplexer #(.enable("false")) multiplexer_7 (
    .in0(not_1_out), .in1(and_1_out), .out(multiplexer_7_out[0]), .sel(controlunit_1_out_16));
  or Jump_R (multiplexer_7_out[1], alu_control_1_out_7, controlunit_1_out_4);
  Multiplexer #(.select(2), .width(32), .enable("false")) multiplexer_8 (
    .in0(adder_1_out), .in1(adder_2_out), .in2(multiplexer_6_out), .in3(multiplexer_6_out),
    .out(multiplexer_8_out), .sel(multiplexer_7_out));
  SaveByte savebyte_1 (
    .in_2(alu_1_out_9[1:0]), .in_3(registerfile_1_out_7), .in_4(demultiplexer_2_out1),
    .out_6(savebyte_1_out_6), .in_5(controlunit_1_out_15[0]), .in_1(registerfile_1_out_7));
  Multiplexer #(.width(32), .enable("false")) multiplexer_9 (
    .in0(registerfile_1_out_7), .in1(savebyte_1_out_6), .out(multiplexer_9_out), .sel(controlunit_1_out_11));
  DataMemory datamemory_1 (
    .in_2({alu_1_out_9[31:2], 2'b00}), .in_3(multiplexer_9_out), .in_1(controlunit_1_out_7),
    .in_4(controlunit_1_out_5), .out_5(datamemory_1_out_5));
  ByteExtractor byteextractor_1 (
    .in_1(datamemory_1_out_5), .in_2(Signed_out), .in_3(alu_1_out_9[1:0]), .out_4(byteextractor_1_out_4),
    .out_5(byteextractor_1_out_5));
  Multiplexer #(.select(2), .width(32), .enable("false")) multiplexer_10 (
    .in0(alu_1_out_9), .in1(multiplexer_11_out), .in2(multiplexer_5_out), .in3(multiplexer_5_out),
    .out(multiplexer_10_out), .sel(controlunit_1_out_6));
  Demultiplexer #(.width(32), .enable("false")) demultiplexer_2 (
    .out0(demultiplexer_2_out0), .out1(demultiplexer_2_out1), .in(multiplexer_10_out),
    .sel(controlunit_1_out_11));
  Multiplexer #(.select(2), .width(32), .enable("false")) multiplexer_11 (
    .in0(datamemory_1_out_5), .in1(byteextractor_1_out_5), .in2(byteextractor_1_out_4),
    .in3(byteextractor_1_out_4), .out(multiplexer_11_out), .sel(controlunit_1_out_15));
endmodule

module af (
);

  wire alu_control_1_p4, and_1_out, controlunit_1_p1, controlunit_1_p2, controlunit_1_p3, controlunit_1_p4,
       controlunit_1_p5, controlunit_1_p7, controlunit_1_p8, controlunit_1_p9, controlunit_1_p10,
       controlunit_1_p11, controlunit_1_p12, controlunit_1_p13, controlunit_1_p14, controlunit_1_p15,
       controlunit_1_p16, multiplexer_9_out, multiplyunit_1_p3, not_1_out;
  wire [1:0] alu_1_p6;
  wire [4:0] alu_1_p4, multiplexer_1_out, multiplexer_2_out;
  wire [5:0] instructionmemory_1_out_2_2;
  wire [25:0] instructionmemory_1_out_2;
  wire [31:0] adder_1_out, adder_2_out, alu_control_1_p5, byteextractor_1_p4, controlunit_1_p17,
       datamemory_1_out_5, demultiplexer_1_out1, multiplexer_3_out, multiplexer_4_out, multiplexer_6_out,
       multiplexer_7_out, multiplexer_8_out, multiplexer_10_out, multiplexer_11_out, multiplexer_12_out,
       n2bitshift_1_out_2, pc_1_out_2, registerfile_1_out_7, savebyte_1_out_6, signextend1632_1_out_3;
  wire [31:2] alu_1_p6_2;

  InstructionMemory instructionmemory_1 (
    .in_1(pc_1_out_2), .out_2({instructionmemory_1_out_2_2, instructionmemory_1_out_2}));
  PC pc_1 (.in_1(multiplexer_10_out), .out_2(pc_1_out_2));
  Adder #(.width(32)) adder_1 (.a(pc_1_out_2), .b(32'h4), .out(adder_1_out));  // open: cin, cout
  // ControlUnit controlunit_1: pin names not known; wires that end beside it: controlunit_1_p1, controlunit_1_p2, controlunit_1_p3, controlunit_1_p4, controlunit_1_p5, controlunit_1_p4, controlunit_1_p7, controlunit_1_p8, controlunit_1_p9, controlunit_1_p10, controlunit_1_p11, controlunit_1_p12, controlunit_1_p13, controlunit_1_p14, controlunit_1_p15, controlunit_1_p16, controlunit_1_p17
  RegisterFile registerfile_1 (
    .WRITE(controlunit_1_p9), .Write_Data(multiplexer_3_out), .in_3(multiplexer_2_out),
    .in_4(instructionmemory_1_out_2[25:21]), .in_5(instructionmemory_1_out_2[20:16]),
    .out_6(controlunit_1_p17), .out_7(registerfile_1_out_7));
  Multiplexer #(.width(5), .enable("false")) multiplexer_1 (
    .in0(instructionmemory_1_out_2[20:16]), .in1(instructionmemory_1_out_2[15:11]), .out(multiplexer_1_out),
    .sel(controlunit_1_p1));
  Multiplexer #(.width(5), .enable("false")) multiplexer_2 (
    .in0(multiplexer_1_out), .in1({5{1'b1}}), .out(multiplexer_2_out), .sel(controlunit_1_p14));
  Multiplexer #(.width(32), .enable("false")) multiplexer_3 (
    .in0(alu_control_1_p5), .in1(multiplexer_10_out), .out(multiplexer_3_out), .sel(controlunit_1_p14));
  SignExtend1632 signextend1632_1 (
    .in_1(instructionmemory_1_out_2[15:0]), .in_2(controlunit_1_p12), .out_3(signextend1632_1_out_3));
  // ALU_Control alu_control_1: pin names not known; wires that end beside it: controlunit_1_p9, instructionmemory_1_out_2[5:0], controlunit_1_p4, alu_control_1_p4, alu_control_1_p5, controlunit_1_p2
  // MultiplyUnit multiplyunit_1: pin names not known; wires that end beside it: controlunit_1_p17, controlunit_1_p15, multiplyunit_1_p3
  Multiplexer #(.width(32), .enable("false")) multiplexer_4 (
    .in0(registerfile_1_out_7), .in1(signextend1632_1_out_3), .out(multiplexer_4_out), .sel(controlunit_1_p8));
  // ALU alu_1: pin names not known; wires that end beside it: controlunit_1_p17, multiplexer_4_out, alu_control_1_p4, alu_1_p4, multiplyunit_1_p3, {alu_1_p6_2, alu_1_p6}, {alu_1_p6_2, alu_1_p6}
  Multiplexer #(.width(5), .enable("false")) multiplexer_5 (
    .in0({5{1'b0}}), .in1(signextend1632_1_out_3[10:6]), .out(alu_1_p4), .sel(controlunit_1_p13));
  Multiplexer #(.width(32), .enable("false")) multiplexer_6 (
    .in0({adder_1_out[31:28], instructionmemory_1_out_2_2[1:0], instructionmemory_1_out_2[25:2], adder_1_out[1:0]}),
    .in1(controlunit_1_p17), .out(multiplexer_6_out), .sel(controlunit_1_p15));
  _2BitShift u_2bitshift_1 (.in_1(signextend1632_1_out_3), .out_2(n2bitshift_1_out_2));
  SaveByte savebyte_1 (
    .in_2(alu_1_p6), .in_4(demultiplexer_1_out1), .out_6(savebyte_1_out_6), .in_1(registerfile_1_out_7));  // open: in_3, in_5
  Adder #(.width(32)) adder_2 (.a(adder_1_out), .b(n2bitshift_1_out_2), .out(adder_2_out));  // open: cin, cout
  Multiplexer #(.width(32), .enable("false")) multiplexer_7 (
    .in0(registerfile_1_out_7), .in1(savebyte_1_out_6), .out(multiplexer_7_out), .sel(controlunit_1_p10));
  not not_1 (not_1_out, and_1_out);
  and and_1 (and_1_out, controlunit_1_p3, multiplyunit_1_p3);
  DataMemory datamemory_1 (
    .in_2({alu_1_p6_2, 2'b00}), .in_3(multiplexer_7_out), .out_5(datamemory_1_out_5));  // open: in_1, in_4
  Multiplexer #(.width(32), .enable("false")) multiplexer_8 (
    .in0(adder_1_out), .in1(adder_2_out), .out(multiplexer_8_out), .sel(multiplexer_9_out));
  Multiplexer #(.enable("false")) multiplexer_9 (
    .in0(not_1_out), .in1(and_1_out), .out(multiplexer_9_out), .sel(controlunit_1_p16));
  Multiplexer #(.width(32), .enable("false")) multiplexer_10 (
    .in0(multiplexer_8_out), .in1(multiplexer_6_out), .out(multiplexer_10_out), .sel(controlunit_1_p2));
  // ByteExtractor byteextractor_1: pin names not known; wires that end beside it: datamemory_1_out_5, alu_1_p6, controlunit_1_p12, byteextractor_1_p4
  Multiplexer #(.width(32), .enable("false")) multiplexer_11 (
    .in0({alu_1_p6_2, alu_1_p6}), .in1(multiplexer_12_out), .out(multiplexer_11_out), .sel(controlunit_1_p5));
  Demultiplexer #(.width(32), .enable("false")) demultiplexer_1 (
    .out0(alu_control_1_p5), .out1(demultiplexer_1_out1), .in(multiplexer_11_out), .sel(controlunit_1_p11));
  Multiplexer #(.width(32), .enable("false")) multiplexer_12 (
    .in0(datamemory_1_out_5), .in1(byteextractor_1_p4), .out(multiplexer_12_out), .sel(controlunit_1_p10));
endmodule

module MultiplyUnit (
  input  [31:0] in_1,
  input  [31:0] in_2,
  input  [31:0] in_3,
  input  [31:0] in_4,
  input  in_5,
  input  in_6,
  input  in_7,
  input  in_8,
  output [31:0] out_9,
  output [31:0] out_10
);
endmodule

module SignExtend1632 (
  input  [15:0] in_1,
  input  in_2,
  output [31:0] out_3
);

  wire [31:0] bit_extender_1_out, bit_extender_2_out;

  assign bit_extender_1_out = {{16{1'b0}}, in_1};  // Bit_Extender bit_extender_1
  assign bit_extender_2_out = {{16{in_1[15]}}, in_1};  // Bit_Extender bit_extender_2
  Multiplexer #(.width(32), .enable("false")) multiplexer_1 (
    .in0(bit_extender_1_out), .in1(bit_extender_2_out), .out(out_3), .sel(in_2));
endmodule

module ByteExtractor (
  input  [31:0] in_1,
  input  in_2,
  input  [1:0] in_3,
  output [31:0] out_4,
  output [31:0] out_5
);

  wire [1:0] not_1_out;
  wire [7:0] multiplexer_1_out;

  assign not_1_out = ~in_3;  // NOT_Gate not_1, 2 bits wide
  Sign_Extend sign_extend_1 (.in_1(multiplexer_1_out), .in_2(in_2), .out_3(out_4));
  Multiplexer #(.select(2), .width(8), .enable("false")) multiplexer_1 (
    .in0(in_1[7:0]), .in1(in_1[15:8]), .in2(in_1[23:16]), .in3(in_1[31:24]), .out(multiplexer_1_out),
    .sel(not_1_out));
endmodule

module SaveByte (
  input  [31:0] in_1,
  input  [1:0] in_2,
  input  [31:0] in_3,
  input  [31:0] in_4,
  input  in_5,
  output [31:0] out_6
);

  wire [1:0] not_1_out;
  wire [31:0] and_1_out, multiplexer_1_out, multiplexer_2_out, multiplexer_3_out, multiplexer_4_out,
       shifter_1_out, shifter_2_out, shifter_3_out;

  Multiplexer #(.select(2), .width(32), .enable("false")) multiplexer_1 (
    .in0(32'hffffff), .in1(32'hff00ffff), .in2(32'hffff00ff), .in3(32'hffffff00), .out(multiplexer_1_out),
    .sel(not_1_out));
  Multiplexer #(.width(32), .enable("false")) multiplexer_2 (
    .in0(in_3), .in1(shifter_1_out), .out(multiplexer_2_out), .sel(not_1_out[1]));
  Shifter #(.width(32)) shifter_1 (.in(in_3), .\dist (5'b01000), .out(shifter_1_out));
  assign and_1_out = in_4 & multiplexer_1_out;  // AND_Gate and_1, 32 bits wide
  Multiplexer #(.width(32), .enable("false")) multiplexer_3 (
    .in0(multiplexer_2_out), .in1(shifter_2_out), .out(multiplexer_3_out), .sel(not_1_out[1]));
  Shifter #(.width(32)) shifter_2 (.in(multiplexer_2_out), .\dist (5'b01000), .out(shifter_2_out));
  Multiplexer #(.width(32), .enable("false")) multiplexer_4 (
    .in0(multiplexer_3_out), .in1(shifter_3_out), .out(multiplexer_4_out), .sel(not_1_out[0]));
  Shifter #(.width(32)) shifter_3 (.in(multiplexer_3_out), .\dist (5'b01000), .out(shifter_3_out));
  assign not_1_out = ~in_2;  // NOT_Gate not_1, 2 bits wide
  assign out_6 = multiplexer_4_out | and_1_out;  // OR_Gate or_1, 32 bits wide
endmodule
